# Fritzing sketch UNO sketch (saved by Fritzing 0.9.3b)
circuit board: 10.6484cm x 18.6779cm

parts:
  Componente3 = Bluetooth HC-05 Macho
  R1 = Resistor [tolerance=±5% resistance=220 package=THT]
  SparkFun1 = SoftPot Membrane Potentiometer - 50mm [part_number=SEN-08680]
  SparkFun2 = SoftPot Membrane Potentiometer - 50mm [part_number=SEN-08680]
  SparkFun3 = SoftPot Membrane Potentiometer - 50mm [part_number=SEN-08680]
  R3 = Resistor [tolerance=±5% resistance=10k package=THT]  # not connected
  R4 = Resistor [tolerance=±5% resistance=10k package=THT]
  R5 = Resistor [tolerance=±5% resistance=10k package=THT]  # not connected
  Componente2 = Thumb Joystick
  Componente4 = Arduino Uno (Rev3)
  X2 = USB Connectors [package=usb-a-s-silk-female]
  X3 = USB Connectors [package=usb-a-s-silk-female]
  R14 = Resistor [tolerance=±5% resistance=10k package=THT]
  DIN1 = DIN-5 jack (MIDI) [package=THT]
  X4 = USB Connectors [package=usb-microb]
  R2 = Resistor [tolerance=±5% resistance=220 package=THT]

nets:
  N1: Componente3.TXD, Componente4.D4
  N2: Componente3.RXD, Componente4.D5_PWM
  GND: Componente3.VCC, SparkFun1.leg1, SparkFun2.leg1, SparkFun3.leg1, Componente4.5V
  GND_2: Componente3.GND, Componente2.GND, Componente4.GND
  N3: R1.Pin_0, Componente4.D3_PWM
  N4: R1.Pin_1, DIN1.4
  N5: SparkFun1.wiper, Componente4.A4/SDA
  N6: SparkFun1.leg2, SparkFun2.leg2, SparkFun3.leg2
  N7: SparkFun2.wiper, R4.Pin_1
  N8: SparkFun3.wiper, Componente4.A2, R14.Pin_1
  N9: Componente2.SEL, Componente4.D8
  N10: Componente2.HORZ, Componente4.A1
  N11: Componente2.VERT, Componente4.A0
  N12: Componente2.VCC, R2.Pin_1
  N13: X2.D+, X3.D+
  N14: X3.D-, X4.GND
  N15: DIN1.5, R2.Pin_0

notes:
  Cables de puenteado
  Main GND:
  R8
  Js:
  R6
  R7
  R13
  Softpot:
  R10
  R11
  R12
  Pins:
  6, 7 (RX, TX TFT LCD)
  9, 10, 11(RGB LEDs)
  Por agregar:
  Pines pantalla
  Pines LEDs
  Visual Music Z
  TX and RT for the Nextion TFT Display
  USB ports for powering the Arduino and the MIDI module
  The powerbank is connected here

custom parts:
  SoftPot Membrane Potentiometer - 50mm: These are very thin variable potentiometers. By pressing down on various parts of the strip, the resistance linearly changes from 100Ohms to 10,000Ohms allowing the user to very accurately calculate the relative position on the strip. Can be used as an accurate positional indicator for CNC head positioning, variable user input (volume level input for example), straight user input (multiple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

// code stored in the sketch: inputsRead.ino
void inputsRead()
{
  if(btmodule.available())
  {
    btdata = btmodule.read();
  }
  
  fret1New = map(analogRead(string1Pin), 0, 950, 0, 22);    //String 1 analog input mapping
  fret1New = constrain(fret1New, 0, 22);
  fret2New = map(analogRead(string2Pin), 0, 950, 0, 22);    //String 1 analog input mapping
  fret2New = constrain(fret2New, 0, 22);
  fret3New = map(analogRead(string3Pin), 0, 950, 0, 22);    //String 1 analog input mapping
  fret3New = constrain(fret3New, 0, 22);
  
  jsxlMap = map(analogRead(jsxPin), 500, 0, 0, 127);    //Joystick horizontal axis left side
  jsxlMap = constrain(jsxlMap, 0, 127);
  jsxrMap = map(analogRead(jsxPin), 530, 1023, 0, 127);    //Joystick horizontal axis right side
  jsxrMap = constrain(jsxrMap, 0, 127);
  jsxMapNew = jsxlMap + jsxrMap;    //Joystick horizontal axis total
  jsyuMap = map(analogRead(jsyPin), 500, 0, 0, 127);    //Joystick vetical axis upper side
  jsyuMap = constrain(jsyuMap, 0, 127);
  jsydMap = map(analogRead(jsyPin), 540, 1023, 0, 127);    //Joystick vertical axis down side
  jsydMap = constrain(jsydMap, 0, 127);
  jsyMapNew = jsyuMap + jsydMap;    //Joystick vertical axis total


  sw1StateNew = digitalRead(sw1Pin);    //Switch pins new state

/*
  if(fret1New - fret1Old >= 1 || fret1Old - fret1New >= 1)    //Fret 1 change detection
  {
    fret1Old = fret1New;
    cpctv1New = HIGH;
    
    Serial.print("fret1New on fret change: "); Serial.println(fret1New);
  }

  if(fret2New - fret2Old >= 1 || fret2Old - fret2New >= 1)    //Fret 2 change detection
  {
    fret2Old = fret2New;
    noteSend(144, C2[fret2New], 127);
    
    Serial.print("fret2New on fret change: "); Serial.println(fret2New);
  }

  if(fret3New - fret3Old >= 1 || fret3Old - fret3New >= 1)    //Fret 3 change detection
  {
    fret3Old = fret3New;
    noteSend(144, C3[fret3New], 127);
    
    Serial.print("fret3New on fret change: "); Serial.println(fret3New);
  }
*/  


    

  if(jsxMapNew - jsxMapOld >= 4 || jsxMapOld - jsxMapNew >= 4)
  {
    jsxMapOld = jsxMapNew;
    noteSend(analogParameter1+0, 01, jsxMapNew);
    noteSend(analogParameter1+1, 01, jsxMapNew);
    noteSend(analogParameter1+2, 01, jsxMapNew);
    Serial.print("Js on X: "); Serial.println(jsxMapNew);
  }

  if(jsyMapNew - jsyMapOld >= 4 || jsyMapOld - jsyMapNew >= 4)
  {
    jsyMapOld = jsyMapNew;
    noteSend(analogParameter3+0, 01, jsyMapNew);
    noteSend(analogParameter3+1, 01, jsyMapNew);
    noteSend(analogParameter3+2, 01, jsyMapNew);
    Serial.print("Js on Y: "); Serial.println(jsyMapNew);
  }
 /*
  if(sw1StateNew == HIGH && sw1StateOld == LOW)
  {
    if(sustainState == HIGH)
    {
      noteSend(176, 64, 127);
      noteSend(177, 64, 127);
      noteSend(178, 64, 127);
      sustainState = 0;
    }
    else
    {
      noteSend(176, 64, 00);
      noteSend(177, 64, 00);
      noteSend(178, 64, 00);
      sustainState = 1;
    }
    sw1StateOld = sw1StateNew;
  }
  sw1StateOld = sw1StateNew;
*/

    if(Serial.read() == '1' || btmodule.read() == '1')
    {
      instrument = instrument+1;
      if(instrument >= 32)
      {
        instrument = 24;
      }
      
      shutDownAll();
      noteSend(192,0,instrument);
      noteSend(193,0,instrument);
      noteSend(194,0,instrument);
      btdata = 0;
    }
}

// code stored in the sketch: MIDI_Electronic_Guitar_VisualMusicZ.ino
/*
 * This is the program developed by the Visual Music Z team for making an electronic guitar using an Arduino UNO, to replicate the
 * basic functions of an electric guitar. Our website: http://visualmusicz.com/
 * 
 * It uses a MIDI X3M chip as the sound module, which recieves the MIDI commands to create notes,
 * audio modulation and sound effects, and sends them directly to an AUX output.
 * See MIDI Messages List: https://www.midi.org/specifications-old/item/table-2-expanded-messages-list-status-bytes
 * See MIDI Control Change Messages List: https://www.midi.org/specifications-old/item/table-3-control-change-messages-data-bytes-2
 * 
 * It also uses a Bluetooth communication module (HC-05) to interact with our mobile app to switch between instrument sounds,
 * effects and more options to increase the electronic guitar experience.
 * See BT communication and AT commands explanation video: https://youtu.be/5SmKOUHhmWk?t=240
 * 
 * List of materials used in this project:
 * x1 Generic Arduino UNO Rev3 board
 * x3 Spectra Symbol Softpot Ribbon Sensors (https://www.mouser.com/ProductDetail/Spectra-Symbol/SP-L-0500-203-3-ST?qs=rVuZtzXoae5%2FClXxQbhQtw==)
 * x1 Nextion NX4827T043 HMI TFT LED Touch Display 4.3" (https://nextion.tech/datasheets/nx4827t043/)
 * x1 Generic Joystick Module (https://components101.com/modules/joystick-module)
 * x1 X3M MIDI Sound Module (https://www.excelvalley.com/product/midi-usb-sound-module/)
 * x1 MIDI DIN Female Connector (https://www.sparkfun.com/products/9536)
 * x1 Generic HC-05 Bluetooth Module (http://www.electronica60norte.com/mwfls/pdf/newBluetooth.pdf)
 * x2 220ohms resistors
 * x3 10Kohms resistors
 * x14 Jumper Wires Male to Female
 * x5 RGB LEDs (common anode)
 * 
 * Created by: Alejandro Mendoza Rojas
 * Last edited: 26-08-2020
 */

//--Libraries--//
#include <SoftwareSerial.h>   //Used for communicating the Arduino with the MIDI and Bluetooth modules, and the TFT LED Display 

//--Objects--//
SoftwareSerial mididin(2, 3);   //RX and TX on the Arduino, Pin 3 is the MIDI OUT
SoftwareSerial btmodule(4, 5);    //RX and TX on the Arduino, BT TX to AR RX, BT RX to AR TX
SoftwareSerial tftled(6, 7);    //RX and TX on the Arduino

//--Pins--//
#define jsxPin A0   //Joystick analog pins
#define jsyPin A1

#define sw1Pin 8   //Joystick push button digital input pin

#define string1Pin A2   //Guitar strings analog pins (common anode)
#define string2Pin A3
#define string3Pin A4

#define red 9			//RGB LEDs PWM controller pins
#define green 10
#define blue 11



//--Notes--//
byte DO[10] =     {0, 24, 36, 48, 60, 72, 84, 96,108,120};
byte DO_S[10] =   {0, 25, 37, 49, 61, 73, 85, 97,109,121};
byte RE[10] =     {0, 26, 38, 50, 62, 74, 86, 98,110,122};
byte RE_S[10] =   {0, 27, 39, 51, 63, 75, 87, 99,111,123};
byte MI[10] =     {0, 28, 40, 52, 64, 76, 88,100,112,124};
byte FA[10] =     {0, 29, 41, 53, 65, 77, 89,101,113,125};
byte FA_S[10] =   {0, 30, 42, 54, 66, 78, 90,102,114,126};
byte SOL[10] =    {0, 31, 43, 55, 67, 79, 91,103,115,127};
byte SOL_S[10] =  {0, 32, 44, 56, 68, 80, 92,104,116,  0};
byte LA[10] =     {0, 33, 45, 57, 69, 81, 93,105,117,  0};
byte LA_S[10] =   {0, 34, 46, 58, 70, 82, 94,106,118,  0};
byte SI[10] =     {0, 35, 47, 59, 71, 83, 95,107,119,  0};

int C1[23] = {SOL[2], FA[4], MI[4], RE_S[4], RE[4], DO_S[4], DO[4], SI[3], LA_S[3], LA[3], SOL_S[3], SOL[3], FA_S[3], FA[3], MI[3], RE_S[3], RE[3], DO_S[3], DO[3], SI[2], LA_S[2], LA[2], SOL_S[2]};
int C2[23] = {SI[2], LA_S[4], LA[4], SOL_S[4], SOL[4], FA[4], MI[4], RE_S[4], RE[4], DO_S[4], DO[4], SI[3], LA_S[3], LA[3], SOL_S[3], SOL[3], FA_S[3], FA[3], MI[3], RE_S[3], RE[3], DO_S[3], DO[3]};
int C3[23] = {MI[3], RE_S[5], RE[5], DO_S[5], DO[5], SI[4], LA_S[4], LA[4], SOL_S[4], SOL[4], FA[4], MI[4], RE_S[4], RE[4], DO_S[4], DO[4], SI[3], LA_S[3], LA[3], SOL_S[3], SOL[3], FA_S[3], FA[3]};

//--Variables--//
int jsxlMap = 0;    //For the Joystick
int jsxrMap = 0;
int jsyuMap = 0;
int jsydMap = 0;
int jsxMapOld = 0;
int jsxMapNew = 0;
int jsyMapOld = 0;
int jsyMapNew = 0;

int fret1New = 0;   //Fret variables for each guitar string
int fret1Old = 0;
int fret2New = 0;
int fret2Old = 0;
int fret3New = 0;
int fret3Old = 0;

int cpctv1New = 0;
int cpctv1Old = 0;
int cpctv2New = 0;
int cpctv2Old = 0;
int cpctv3New = 0;
int cpctv3Old = 0;

bool cpctv1State = LOW;   /iir 12u308'2
bool cpctv2State = LOW;
bool cpctv3State = LOW;

bool sw1StateOld = HIGH;    //Button states
bool sw1StateNew = HIGH;

byte analogParameter1 = 176;    //Function message to send (intended for analog input devices)
byte analogParameter2 = 176;
byte analogParameter3 = 224;

/*
 * cmd 144: note on
 * cmd 128: note off
 * cmd 176 01: control change ¬¬¬¬¬¬¬¬¬¬¬¬¬¬
 * cmd 176 64: sustain
 * cmd 176 91: depth reverb
 * cmd 176 126: mono mode
 * cmd 192: program/instrument change
 * cmd 224: pitch bend change ¬¬¬¬¬¬¬¬¬¬¬¬¬¬¬¬¬
 */

//--Instruments--//
byte instrument = 24;   //Default
/*
 * Guitars:
 * 24 - Acustic guitar (nylon)
 * 25 - Acustic guitar (steel)
 * 26 - Electric guitar (jazz)
 * 27 - Electric guitar (clean)
 * 28 - Electric guitar (muted)
 * 29 - Overdriven guitar
 * 30 - Distortion guitar
 * 31 - Guitar harmonics
 * See MIDI Instruments list: http://fmslogo.sourceforge.net/manual/midi-instrument.html
 */

char btdata = ' ';


 
void setup() {
  Serial.begin(9600);   //Initializing the Serial communication with devices
  mididin.begin(31250);
  btmodule.begin(9600);
  pinMode(sw1Pin, INPUT_PULLUP);
	pinMode(red, OUTPUT);
	pinMode(green, OUTPUT);
	pinMode(blue, OUTPUT);
  noteSend(192, 00, instrument);    //Assign the same instrument for channels 1-3
  noteSend(193, 00, instrument);
  noteSend(194, 00, instrument);
  delay(100);
  noteSend(176, 91, 127);   //Reverb enabled for channels 1-3
  noteSend(177, 91, 127);
  noteSend(178, 91, 127);
  delay(100);
  noteSend(176, 126, 00);   //Mono Mode On for channels 1-3
  noteSend(177, 126, 00);
  noteSend(178, 126, 00);
  delay(100);
  noteSend(176, 65, 00);   //Portamento ON for channels 1-3
  noteSend(177, 65, 00);
  noteSend(178, 65, 00);
  delay(100);
}

void loop() {
  inputsRead();
}

// code stored in the sketch: MIDI_Modulation_Finale.ino
/*
 * This program is intended to be used with an Arduino MEGA to replicate the basic functions of an electric guitar.
 * It's also intended to communicate with a MIDI X3M chip (See website https://www.excelvalley.com/product/midi-usb-sound-module/),
 * which recieves the MIDI commands to create notes, audio modulation and sound effects. At last, it also uses a
 * Bluetooth communication module (HC-05) to interact with our mobile app to switch between instrument sounds,
 * effects and more options to increase the electronic guitar experience.
 * See MIDI Messages List: https://www.midi.org/specifications-old/item/table-2-expanded-messages-list-status-bytes
 * See MIDI Control Change Messages List: https://www.midi.org/specifications-old/item/table-3-control-change-messages-data-bytes-2
 * Created by: Alejandro Mendoza Rojas
 * Last edited: 19-08-2020
 */

//--Libraries--//
#include <SoftwareSerial.h>   //Used for communicating with the MIDI module

//--Objects--//
SoftwareSerial mididin(2, 3);   //Pin 3 is the MIDI OUT
SoftwareSerial btmodule(4, 5);    //RX, TX on Arduino

//--Pins--//
#define jsxPin = A0;   //Joystick analog pins
#define jsyPin = A1;

#define sw1Pin = 8;    //Joystick push button digital input pin

#define string1Pin = A2;   //Guitar strings analog pins
#define string2Pin = A3;
#define string3Pin = A4;

#define capacitive1Pin = 11;    //Capacitive touch digital sensors input pins
#define capacitive2Pin = 10;
#define capacitive3Pin = 9;



//--Notes--//
byte DO[10] =     {0, 24, 36, 48, 60, 72, 84, 96,108,120};
byte DO_S[10] =   {0, 25, 37, 49, 61, 73, 85, 97,109,121};
byte RE[10] =     {0, 26, 38, 50, 62, 74, 86, 98,110,122};
byte RE_S[10] =   {0, 27, 39, 51, 63, 75, 87, 99,111,123};
byte MI[10] =     {0, 28, 40, 52, 64, 76, 88,100,112,124};
byte FA[10] =     {0, 29, 41, 53, 65, 77, 89,101,113,125};
byte FA_S[10] =   {0, 30, 42, 54, 66, 78, 90,102,114,126};
byte SOL[10] =    {0, 31, 43, 55, 67, 79, 91,103,115,127};
byte SOL_S[10] =  {0, 32, 44, 56, 68, 80, 92,104,116,  0};
byte LA[10] =     {0, 33, 45, 57, 69, 81, 93,105,117,  0};
byte LA_S[10] =   {0, 34, 46, 58, 70, 82, 94,106,118,  0};
byte SI[10] =     {0, 35, 47, 59, 71, 83, 95,107,119,  0};

int C1[23] = {SOL[2], FA[4], MI[4], RE_S[4], RE[4], DO_S[4], DO[4], SI[3], LA_S[3], LA[3], SOL_S[3], SOL[3], FA_S[3], FA[3], MI[3], RE_S[3], RE[3], DO_S[3], DO[3], SI[2], LA_S[2], LA[2], SOL_S[2]};
int C2[23] = {SI[2], LA_S[4], LA[4], SOL_S[4], SOL[4], FA[4], MI[4], RE_S[4], RE[4], DO_S[4], DO[4], SI[3], LA_S[3], LA[3], SOL_S[3], SOL[3], FA_S[3], FA[3], MI[3], RE_S[3], RE[3], DO_S[3], DO[3]};
int C3[23] = {MI[3], RE_S[5], RE[5], DO_S[5], DO[5], SI[4], LA_S[4], LA[4], SOL_S[4], SOL[4], FA[4], MI[4], RE_S[4], RE[4], DO_S[4], DO[4], SI[3], LA_S[3], LA[3], SOL_S[3], SOL[3], FA_S[3], FA[3]};

//--Variables--//
int jsxlMap = 0;    //For the Joystick
int jsxrMap = 0;
int jsyuMap = 0;
int jsydMap = 0;
int jsxMapOld = 0;
int jsxMapNew = 0;
int jsyMapOld = 0;
int jsyMapNew = 0;

int fret1New = 0;   //Fret variables for each guitar string
int fret1Old = 0;
int fret2New = 0;
int fret2Old = 0;
int fret3New = 0;
int fret3Old = 0;

int cpctv1New = 0;
int cpctv1Old = 0;
int cpctv2New = 0;
int cpctv2Old = 0;
int cpctv3New = 0;
int cpctv3Old = 0;

bool cpctv1State = LOW;   /iir 12u308'2
bool cpctv2State = LOW;
bool cpctv3State = LOW;

bool sw1StateOld = HIGH;    //Button states
bool sw1StateNew = HIGH;

byte analogParameter1 = 176;    //Function message to send (intended for analog input devices)
byte analogParameter2 = 176;
byte analogParameter3 = 224;

/*
 * cmd 144: note on
 * cmd 128: note off
 * cmd 176 01: control change ¬¬¬¬¬¬¬¬¬¬¬¬¬¬
 * cmd 176 64: sustain
 * cmd 176 91: depth reverb
 * cmd 176 126: mono mode
 * cmd 192: program/instrument change
 * cmd 224: pitch bend change ¬¬¬¬¬¬¬¬¬¬¬¬¬¬¬¬¬
 */

//--Instruments--//
byte instrument = 24;   //Default
/*
 * Guitars:
 * 24 - Acustic guitar (nylon)
 * 25 - Acustic guitar (steel)
 * 26 - Electric guitar (jazz)
 * 27 - Electric guitar (clean)
 * 28 - Electric guitar (muted)
 * 29 - Overdriven guitar
 * 30 - Distortion guitar
 * 31 - Guitar harmonics
 * See MIDI Instruments list: http://fmslogo.sourceforge.net/manual/midi-instrument.html
 */

char btdata = ' ';


 
void setup() {
  Serial.begin(9600);   //Initializing the Serial communication with devices
  mididin.begin(31250);
  btmodule.begin(9600);
  pinMode(sw1Pin, INPUT_PULLUP);
  pinMode(sw4Pin, INPUT_PULLUP);
  pinMode(capacitive1Pin, INPUT_PULLUP);
  pinMode(capacitive2Pin, INPUT_PULLUP);
  pinMode(capacitive3Pin, INPUT_PULLUP);
  noteSend(192, 00, instrument);    //Assign the same instrument for channels 1-3
  noteSend(193, 00, instrument);
  noteSend(194, 00, instrument);
  delay(100);
  noteSend(176, 91, 127);   //Reverb enabled for channels 1-3
  noteSend(177, 91, 127);
  noteSend(178, 91, 127);
  delay(100);
  noteSend(176, 126, 00);   //Mono Mode On for channels 1-3
  noteSend(177, 126, 00);
  noteSend(178, 126, 00);
  delay(100);
  noteSend(176, 65, 00);   //Portamento ON for channels 1-3
  noteSend(177, 65, 00);
  noteSend(178, 65, 00);
  delay(100);
}

void loop() {
  inputsRead();
}

// code stored in the sketch: noteSend.ino
void noteSend(char cmd, char data1, char data2)   //MIDI protocol message
{
  mididin.write(cmd);
  mididin.write(data1);
  mididin.write(data2);
}

// code stored in the sketch: noteSendAll.ino
void noteSendAll(char cmd, char data1, char data2)   //MIDI protocol message
{
  for(int u=0;u<=2;u++)
  {
    mididin.write(cmd+u);
    mididin.write(data1);
    mididin.write(data2);
  }
}

// code stored in the sketch: shutDownAll.ino
void shutDownAll()
{
  for(int y=0;y<=22;y++)
  {
    noteSend(128, C1[y], 00);
    noteSend(129, C2[y], 00);
    noteSend(130, C3[y], 00);
  }
}
